# Fritzing sketch Bluetooth.04 (saved by Fritzing 0.9.3b)
breadboards: 1

parts:
  Parça1 = Arduino Uno (Rev3)
  Parça2 = Bluetooth HC-06 Macho
  R1 = Resistor [tolerance=±5% resistance=1k package=THT]
  R2 = Resistor [tolerance=±5% resistance=1k package=THT]
  R3 = Resistor [tolerance=±5% resistance=1k package=THT]
  M1 = DC Motor

nets:
  N1: Parça1.D9_PWM, M1.pin_1
  GND: Parça1.GND, Parça2.GND, R1.Pin_0, M1.pin_2
  N2: Parça1.D6_PWM, R3.Pin_1
  N3: Parça1.D7, Parça2.TXD
  5V: Parça1.5V, Parça2.VCC
  N4: Parça2.RXD, R2.Pin_1, R3.Pin_0
  N5: R1.Pin_1, R2.Pin_0
